// Digital circuit MIPS.dig as structural Verilog
module MIPS (
  input  CLK,
  input  RST,
  output [31:0] PC,
  output [31:0] ALUResult,
  output [31:0] MemData
);

  wire beq, bne, Branch, BranchNe, Jal, Jump, JumpRegister, MemRead, MemToReg, MemWrite, PCSrc, RegWrite,
       zero;
  wire [1:0] ALUSrc, RegDst;
  wire [2:0] ALUOp;
  wire [3:0] Op;
  wire [4:0] RegWAddr;
  wire [5:0] funct;
  wire [9:0] immediate;
  wire [15:0] instr;
  wire [31:0] ALUMem, branch__offset, In1, In2, MemWD, NextPC, NPC0, NPC1, PCBranch, RegWD, sign__imm;
  wire [31:4] PCPlus4;
  wire [31:28] PCJump;

  and and_1 (bne, ~zero, BranchNe);  // And
  and and_2 (beq, zero, Branch);
  or or_1 (PCSrc, bne, beq);
  BarrelShifter #(.Bits(32)) barrelshifter_1 (.in(sign__imm), .shift(6'b000010), .out(branch__offset));
  adder32_1 #(.applicationType("IVERILOG")) u_adder32_1 (.a({PCPlus4, PCJump}), .b(branch__offset), .out(PCBranch));
  Multiplexer #(.Bits(32)) multiplexer_1 (.sel(PCSrc), .in_0({PCPlus4, PCJump}), .in_1(PCBranch), .out(NPC0));
  Multiplexer #(.Bits(32)) multiplexer_2 (.sel(JumpRegister), .in_0(NPC1), .in_1(ALUMem), .out(NextPC));
  adder32_0 #(.applicationType("IVERILOG")) u_adder32_0 (.a(PC), .b(32'h4), .out({PCPlus4, PCJump}));
  Multiplexer #(.Bits(32)) multiplexer_3 (
    .sel(Jump), .in_0(NPC0), .in_1({PCJump, 2'b00, funct, immediate, instr[15:6]}), .out(NPC1));
  BitExtender #(.inputBits(16), .outputBits(32)) bitextender_1 (.in({funct, immediate}), .out(sign__imm));
  Multiplexer #(.Bits(5), .Selector_Bits(2)) multiplexer_4 (
    .sel(RegDst), .in_0(instr[15:11]), .in_1(immediate[4:0]), .in_2(5'b00001), .in_3({5{1'b0}}),
    .out(RegWAddr));
  Multiplexer #(.Bits(32)) multiplexer_5 (.sel(Jal), .in_0({PCPlus4, PCJump}), .in_1(ALUMem), .out(RegWD));
  regfile #(.applicationType("IVERILOG")) u_regfile (
    .Clock(CLK), .Reset(RST), .RegWrite(RegWrite), .ReadAddr1(instr[10:6]), .ReadAddr2(instr[15:11]),
    .WriteAddr(RegWAddr), .WriteData(RegWD), .ReadData1(In1), .ReadData2(MemWD));
  d_mem #(.applicationType("IVERILOG")) u_d_mem (
    .MemWrite(MemWrite), .MemRead(MemRead), .Address(ALUResult), .WriteData(MemWD), .ReadData(MemData));
  PC #(.applicationType("IVERILOG")) u_PC (.Clock(CLK), .NextPC(NextPC), .PC(PC));
  i_mem #(.applicationType("IVERILOG")) u_i_mem (.address(PC), .i_out({funct, immediate, instr}));
  Multiplexer #(.Bits(32), .Selector_Bits(2)) multiplexer_6 (
    .sel(ALUSrc), .in_0(MemWD), .in_1(sign__imm), .in_2({funct, immediate, {16{1'b0}}}),
    .in_3({{16{1'b0}}, funct, immediate}), .out(In2));
  ctrl #(.applicationType("IVERILOG")) u_ctrl (
    .opcode(instr[5:0]), .ALUOp(ALUOp), .RegDst(RegDst), .ALUSrc(ALUSrc), .MemToReg(MemToReg),
    .MemWrite(MemWrite), .MemRead(MemRead), .RegWrite(RegWrite), .Jal(Jal), .Jump(Jump), .BranchNe(BranchNe),
    .Branch(Branch));
  alu #(.applicationType("IVERILOG")) u_alu (.OP(Op), .In1(In1), .In2(In2), .result(ALUResult), .Zero_flag(zero));
  ula_ctrl #(.applicationType("IVERILOG")) u_ula_ctrl (.funct(funct), .ALUOp(ALUOp), .Jr(JumpRegister), .OP(Op));
  Multiplexer #(.Bits(32)) multiplexer_7 (.sel(MemToReg), .in_0(ALUResult), .in_1(MemData), .out(ALUMem));

  // Other names for the same wires on the sheet: opcode[5:0] = instr[5:0];
  //   j__address[25:0] = {funct, immediate, instr[15:6]}; PCJump[25:0] = {funct, immediate, instr[15:6]};
  //   RegAddr1[4:0] = instr[10:6]; rs[4:0] = instr[10:6]; s__j__addr[25:0] = {funct, immediate, instr[15:6]};
  //   RegAddr2[4:0] = instr[15:11]; rt[4:0] = instr[15:11]; instr[31:16] = {funct, immediate};
  //   rd[4:0] = immediate[4:0]; upper__imm[15:0] = {funct, immediate}; zero__imm[31:16] = {funct, immediate};
  //   shamt[4:0] = immediate[9:5]; immediate[15:10] = funct; ALUOut[31:0] = ALUResult; MemAddr[31:0] = ALUResult;
  //   PCPlus4[3:0] = PCJump; RegData1[31:0] = In1; RegData2[31:0] = MemWD

  // Notes on the sheet:
  //   Cálculo do PCSrc
  //   Cálculo PCBranch
  //   Clock, Reset e Outputs
  //   Atualização do PC
  //   Cálculo PCJump
  //   Parse das Instruções de 32-bits
  //   Entradas do regifle
  //   Entradas do ALU
  //   Módulos Verilog
  //   Entradas da d\_mem
  //   ALUMem
endmodule

/* Code of adder32_1:
module adder32_1(
   input [31:0] a, 
   b,
   output [31:0] out);

   assign out = a + b;
endmodule
*/

/* Code of adder32_0:
module adder32_0(
   input [31:0] a, 
   b,
   output [31:0] out);

   assign out = a + b;
endmodule
*/

/* Code of regfile:
// Esse módulo implementa um regfile

module regfile (
        input Clock,
        input Reset,
        input RegWrite,
        input [4:0] ReadAddr1,
        input [4:0] ReadAddr2,
        input [4:0] WriteAddr,
        input [31:0] WriteData,
        output [31:0] ReadData1,
        output [31:0] ReadData2);

    // 32 Registradores de 32 bits
    reg [31:0] Registers [31:0];

    // Inteiro auxiliar para fazer o loop
    //  nos registradores
    integer i;

    always @(posedge Clock or posedge Reset) begin
        if(Reset) begin
            for (i = 0; i < 32; i = i + 1) begin
                Registers[i] <= 32'b0;
            end
        end
        else begin
            if(RegWrite && WriteAddr != 32'b0) begin
                Registers[WriteAddr] <= WriteData;
            end
        end
    end

    assign ReadData1 = (ReadAddr1 == 0) ? 32'b0 : Registers[ReadAddr1];
    assign ReadData2 = (ReadAddr2 == 0) ? 32'b0 : Registers[ReadAddr2];
endmodule
*/

/* Code of d_mem:
/* Esse módulo implementa uma memória de dados
  Vamos utilizar o layout do MIPS presente descrito em: 
    http://www.it.uu.se/education/course/homepage/os/vt18/module-0/mips-and-mars/mips-memory-layout/
* /

module d_mem(
      input MemWrite,
      input MemRead,
      input [31:0] Address,
      input [31:0] WriteData,
      output [31:0] ReadData);

    // Memória RAM
    reg [31:0] RAM [255:0];

    // Inteiro auxiliar para fazer o loop 
    //  nas células de memória
    integer i;
    

    initial begin
      for (i = 0; i < 256; i = i + 1) begin
        RAM[i] <= 32'b0;
      end
    end

    // Escrita na memória
    always @(*) begin
      if (MemWrite) begin
        RAM[Address] <= WriteData;
      end
    end 

    // Leitura dos dados
    assign ReadData = (MemRead == 0) ? 32'b0 : RAM[Address];

endmodule
*/

/* Code of PC:
module PC(input Clock, input [31:0] NextPC, output reg [31:0] PC);

always @(posedge Clock) begin
  PC <= NextPC;
end

endmodule
*/

/* Code of i_mem:
module i_mem(
        input		[31:0]	address ,
        output reg		[31:0]	i_out
    );

    reg [31:0] instructions [255:0];

    initial begin
        $readmemb("instruction.list", instructions);
    end

    always @ (address) begin
        i_out = instructions[address];
    end

endmodule
*/

/* Code of ctrl:
// Módulo de controle que suporta todas as instruções solicitadas.
/* Referências:
- https://www.d.umn.edu/~gshute/mips/control-signal-summary.html
- https://courses.cs.washington.edu/courses/cse378/09wi/lectures/lec08.pdf
* /

module ctrl(
        input [5:0] opcode,
        output reg [2:0] ALUOp,
        output reg [1:0] RegDst,
        ALUSrc,
        output reg MemToReg,
        MemWrite,
        MemRead,
        RegWrite,
        Jal,
        Jump,
        BranchNe,
        Branch);

    always @(*)
    begin
        case(opcode)
            // sll, srl, sra, sllv, srlv, srav, jr, add,
            // sub, and, or, xor, nor, slt, sltu
            6'd0: begin
                ALUOp <= 3'b110;
                MemToReg <= 1'b0;
                RegDst <= 2'b01;
                ALUSrc <= 2'b00;
                MemWrite <= 1'b0;
                MemRead <= 1'b0;
                RegWrite <= 1'b1;
                Jal <= 1'b0;
                Jump <= 1'b0;
                BranchNe <= 1'b0;
                Branch <= 1'b0;
            end
            6'd4: begin // beq
                ALUOp <= 3'b001;
                MemToReg <= 1'bX;
                RegDst <= 2'bXX;
                ALUSrc <= 2'b00;
                MemWrite <= 1'b0;
                MemRead <= 1'b0;
                RegWrite <= 1'b0;
                Jal <= 1'b0;
                Jump <= 1'b0;
                BranchNe <= 1'b0;
                Branch <= 1'b1;
            end
            6'd5: begin // bne
                ALUOp <= 3'b001;
                MemToReg <= 1'bX;
                RegDst <= 2'bXX;
                ALUSrc <= 2'b00;
                MemWrite <= 1'b0;
                MemRead <= 1'b0;
                RegWrite <= 1'b0;
                Jal <= 1'b0;
                BranchNe <= 1'b1;
                Branch <= 1'b0;
            end
            6'd8: begin // addi
                ALUOp <= 3'b000;
                MemToReg <= 1'b0;
                RegDst <= 2'b00;
                ALUSrc <= 2'b01;
                MemWrite <= 1'b0;
                MemRead <= 1'b0;
                RegWrite <= 1'b1;
                Jal <= 1'b0;
                BranchNe <= 1'b0;
                Branch <= 1'b0;
            end
            6'd9, 6'd11: begin // slti, sltiu
                ALUOp <= 3'b101;
                MemToReg <= 1'b0;
                RegDst <= 2'b00;
                ALUSrc <= 2'b01;
                MemWrite <= 1'b0;
                MemRead <= 1'b0;
                RegWrite <= 1'b1;
                Jal <= 1'b0;
                BranchNe <= 1'b0;
                Branch <= 1'b0;
            end
            6'd12: begin // andi
                ALUOp <= 3'b010;
                MemToReg <= 1'b0;
                RegDst <= 2'b00;
                ALUSrc <= 2'b10;
                MemWrite <= 1'b0;
                MemRead <= 1'b0;
                RegWrite <= 1'b1;
                Jal <= 1'b0;
                BranchNe <= 1'b0;
                Branch <= 1'b0;
            end
            6'd13: begin // ori
                ALUOp <= 3'b011;
                MemToReg <= 1'b0;
                RegDst <= 2'b00;
                ALUSrc <= 2'b10;
                MemWrite <= 1'b0;
                MemRead <= 1'b0;
                RegWrite <= 1'b1;
                Jal <= 1'b0;
                BranchNe <= 1'b0;
                Branch <= 1'b0;
            end
            6'd14: begin // xori
                ALUOp <= 3'b100;
                MemToReg <= 1'b0;
                RegDst <= 2'b00;
                ALUSrc <= 2'b10;
                MemWrite <= 1'b0;
                MemRead <= 1'b0;
                RegWrite <= 1'b1;
                Jal <= 1'b0;
                BranchNe <= 1'b0;
                Branch <= 1'b0;
            end
            6'd15: begin // lui
                ALUOp <= 3'b000;
                MemToReg <= 1'b0;
                RegDst <= 2'b00;
                ALUSrc <= 2'b11;
                MemWrite <= 1'b0;
                MemRead <= 1'b0;
                RegWrite <= 1'b1;
                Jal <= 1'b0;
                BranchNe <= 1'b0;
                Branch <= 1'b0;
            end
            6'd35: begin // lw
                ALUOp <= 3'b000;
                MemToReg <= 1'b1;
                RegDst <= 2'b00;
                ALUSrc <= 2'b01;
                MemWrite <= 1'b0;
                MemRead <= 1'b1;
                RegWrite <= 1'b1;
                Jal <= 1'b0;
                BranchNe <= 1'b0;
                Branch <= 1'b0;
            end
            6'd43: begin // sw
                ALUOp <= 3'b000;
                MemToReg <= 1'bX;
                RegDst <= 2'bXX;
                ALUSrc <= 2'b01;
                MemWrite <= 1'b1;
                MemRead <= 1'b0;
                RegWrite <= 1'b0;
                Jal <= 1'b0;
                BranchNe <= 1'b0;
                Branch <= 1'b0;
            end
            6'd2: begin // j
                ALUOp <= 3'bXXX;
                MemToReg <= 1'bX;
                RegDst <= 2'bXX;
                ALUSrc <= 2'bXX;
                MemWrite <= 1'b0;
                MemRead <= 1'b0;
                RegWrite <= 1'b0;
                Jal <= 1'b0;
                Jump <= 1'b1;
                BranchNe <= 1'bX;
                Branch <= 1'bX;
            end
            6'd3: begin // jal
                ALUOp <= 3'bXXX;
                MemToReg <= 1'bX;
                RegDst <= 2'b10;
                ALUSrc <= 2'bXX;
                MemWrite <= 1'b0;
                MemRead <= 1'b0;
                RegWrite <= 1'b1;
                Jal <= 1'b1;
                Jump <= 1'b1;
                BranchNe <= 1'bX;
                Branch <= 1'bX;
            end
        endcase
    end
endmodule
*/

/* Code of alu:
module alu(
        input		[3:0]	OP,
        input		[31:0]	In1, In2,
        output reg	[31:0]	result,
        output				Zero_flag);

    assign Zero_flag = (result == 0);

    always @(*) begin
        case (OP)
            4'b0000: result <= In1 + In2;				/* add * /
            4'b1000: result <= In1 & In2;				/* and * /
            4'b1011: result <= ~(In1 | In2);				/* nor * /
            4'b1001: result <= In1 | In2;				/* or * /
            4'b0001: result <= In1 - In2;					/* sub * /
            4'b1010: result <= In1 ^ In2;				/* xor * /
            4'b0100: result <= In1 << (In2);           /*logical shift left* /
            4'b1100: result <= In1 >> (In2);				 /*logical shift right* /
            4'b1110: result <= (In1 > In2)? 32'd1: 32'd0 ;			 /* comparison* /
            4'b1111: result <= (In1 == In2)? 32'd1: 32'd0 ;  		 /* equal comparison* /

            default: result <= 0;
        endcase
    end

endmodule
*/

/* Code of ula_ctrl:
module ula_ctrl(
        input wire [5:0] funct,
        input wire [2:0] ALUOp,
        output Jr,
        output reg [3:0] OP);

    reg [3:0] OPc;

    always @(*) begin
        case(funct)
            6'b100000, 6'b100001: OPc = 4'b0000; /* add * /
            6'b100010, 6'b100011: OPc = 4'b0001; /* sub * /
            6'b100100: OPc = 4'b1000; /* and * /
            6'b100111: OPc = 4'b1011; /* nor * /
            6'b100101: OPc = 4'b1001; /* or * /
            6'b100010, 6'b100011: OPc = 4'b0001; /* sub * /
            6'b100110: OPc = 4'b1010; /* xor * /
            6'b000000, 6'b000100: OPc = 4'b0100; /* logical shift left * /
            6'b000010, 6'b000111, 6'b000110: OPc = 4'b1100; /* logical shift right * /
            6'b101010, 6'b101011: OPc = 4'b1110; /* comparison * /
            default: OPc = 4'b0000; /* defaults to add * /
        endcase
    end

    always @(*) begin
        case(ALUOp)
            3'b000: OP = 4'b0000; /* add * /
            3'b001: OP = 4'b0001; /* sub * /
            3'b010: OP = 4'b1000; /* and * /
            3'b011: OP = 4'b1001; // or
            3'b100: OP = 4'b1010; // xor
            3'b101: OP = 4'b1110; // slt
            3'b110: OP = OPc; // check funct
            3'b111: OP = 4'b0000; /* N/A, defaults to add * /
            default: OP = 4'b0000; /* defaults to add * /
        endcase
    end

    assign Jr = (ALUOp == 3'b110) ? ((funct == 6'b001000) ? 1'b1 : 1'b0) : 1'b0;

endmodule
*/
